// Logisim project ALU.circ as structural Verilog: 7 circuits, main circuit ALU
module ALU (
  input  [15:0] in_1,
  input  [15:0] in_2,
  input  [2:0] in_3,
  output [15:0] out_4
);

  wire [2:0] comparator_1_gt;
  wire [15:0] adder_1_out, bit_extender_1_out, multiplier_1_out, negator_1_out, shifter_1_out, shifter_2_out,
       subtractor_1_out;

  Adder #(.width(16)) adder_1 (.a(in_1), .b(in_2), .out(adder_1_out));  // open: cin, cout
  Subtractor #(.width(16)) subtractor_1 (.a(in_1), .b(in_2), .out(subtractor_1_out));  // open: bin, bout
  Multiplier #(.width(16)) multiplier_1 (.a(in_1), .b(in_2), .out(multiplier_1_out));  // open: cin, cout
  Shifter #(.width(16)) shifter_1 (.in(in_1), .\dist (in_2[3:0]), .out(shifter_1_out));
  Shifter #(.width(16), .shift("lr")) shifter_2 (.in(in_1), .\dist (in_2[3:0]), .out(shifter_2_out));
  Negator #(.width(16)) negator_1 (.in(in_1), .out(negator_1_out));
  Comparator #(.width(16)) comparator_1 (
    .a(in_1), .b(in_2), .gt(comparator_1_gt[0]), .eq(comparator_1_gt[1]), .lt(comparator_1_gt[2]));
  assign bit_extender_1_out = {{13{1'b0}}, comparator_1_gt};  // Bit_Extender bit_extender_1
  Multiplexer #(.select(3), .width(16)) multiplexer_1 (
    .in0(adder_1_out), .in1(subtractor_1_out), .in2(multiplier_1_out), .in3(shifter_1_out),
    .in4(shifter_2_out), .in5(negator_1_out), .in6(bit_extender_1_out), .out(out_4), .sel(in_3), .en(1'b1));  // open: in7
endmodule

module _16_Bit_summation (
  input  [15:0] Input_a,
  input  [15:0] Input_b,
  input  Subtract,
  output [15:0] Output,
  output Sign
);

  wire and_1_out, n16_bit_adder_1_carry_out;
  wire [15:0] bit_extender_1_out, n16_bit_adder_1_sum, n16_bit_complimentor_1_output,
       n16_bit_complimentor_2_output;

  _16_Bit_complimentor u_16_bit_complimentor_1 (
    .Input(Input_b), .Compliment(Subtract), .Output(n16_bit_complimentor_1_output));
  _16_Bit_adder u_16_bit_adder_1 (
    .Input_a(Input_a), .Carry_in(Subtract), .Input_b(n16_bit_complimentor_1_output),
    .Sum(n16_bit_adder_1_sum), .Carry_out(n16_bit_adder_1_carry_out));
  xor xor_1 (Sign, n16_bit_adder_1_carry_out, Subtract);
  and and_1 (and_1_out, ~n16_bit_adder_1_carry_out, Subtract);  // AND_Gate
  _16_Bit_complimentor u_16_bit_complimentor_2 (
    .Input(n16_bit_adder_1_sum), .Compliment(and_1_out), .Output(n16_bit_complimentor_2_output));
  assign bit_extender_1_out = {{15{1'b0}}, and_1_out};  // Bit_Extender bit_extender_1
  _16_Bit_adder u_16_bit_adder_2 (
    .Input_a(bit_extender_1_out), .Carry_in(1'b0), .Input_b(n16_bit_complimentor_2_output), .Sum(Output));  // open: Carry_out
endmodule

module _16_Bit_complimentor (
  input  [15:0] Input,
  input  Compliment,
  output [15:0] Output
);

  xor xor_1 (Output[0], Input[0], Compliment);
  xor xor_2 (Output[1], Input[1], Compliment);
  xor xor_3 (Output[2], Input[2], Compliment);
  xor xor_4 (Output[3], Input[3], Compliment);
  xor xor_5 (Output[4], Input[4], Compliment);
  xor xor_6 (Output[5], Input[5], Compliment);
  xor xor_7 (Output[6], Input[6], Compliment);
  xor xor_8 (Output[7], Input[7], Compliment);
  xor xor_9 (Output[8], Input[8], Compliment);
  xor xor_10 (Output[9], Input[9], Compliment);
  xor xor_11 (Output[10], Input[10], Compliment);
  xor xor_12 (Output[11], Input[11], Compliment);
  xor xor_13 (Output[12], Input[12], Compliment);
  xor xor_14 (Output[13], Input[13], Compliment);
  xor xor_15 (Output[14], Input[14], Compliment);
  xor xor_16 (Output[15], Input[15], Compliment);
endmodule

module _16_Bit_adder (
  input  [15:0] Input_a,
  input  Carry_in,
  input  [15:0] Input_b,
  output [15:0] Sum,
  output Carry_out
);

  wire n4_bit_adder_1_carry_out, n4_bit_adder_2_carry_out, n4_bit_adder_3_carry_out;

  _4_Bit_adder u_4_bit_adder_1 (
    .Input_a(Input_a[7:4]), .Input_b(Input_b[7:4]), .Sum(Sum[7:4]), .Carry_out(n4_bit_adder_1_carry_out),
    .Carry_in(n4_bit_adder_2_carry_out));
  _4_Bit_adder u_4_bit_adder_2 (
    .Input_a(Input_a[3:0]), .Input_b(Input_b[3:0]), .Sum(Sum[3:0]), .Carry_out(n4_bit_adder_2_carry_out),
    .Carry_in(Carry_in));
  _4_Bit_adder u_4_bit_adder_3 (
    .Input_a(Input_a[11:8]), .Input_b(Input_b[11:8]), .Sum(Sum[11:8]), .Carry_out(n4_bit_adder_3_carry_out),
    .Carry_in(n4_bit_adder_1_carry_out));
  _4_Bit_adder u_4_bit_adder_4 (
    .Input_a(Input_a[15:12]), .Input_b(Input_b[15:12]), .Sum(Sum[15:12]), .Carry_out(Carry_out),
    .Carry_in(n4_bit_adder_3_carry_out));
endmodule

module _4_Bit_adder (
  input  [3:0] Input_a,
  input  Carry_in,
  input  [3:0] Input_b,
  output [3:0] Sum,
  output Carry_out
);

  wire full_adder_1_carry_out, full_adder_2_carry_out, full_adder_3_carry_out;

  Full_adder full_adder_1 (
    .Input_a(Input_a[1]), .Input_b(Input_b[1]), .Carry_in(full_adder_2_carry_out), .Sum(Sum[1]),
    .Carry_out(full_adder_1_carry_out));
  Full_adder full_adder_2 (
    .Input_a(Input_a[0]), .Input_b(Input_b[0]), .Carry_in(Carry_in), .Sum(Sum[0]),
    .Carry_out(full_adder_2_carry_out));
  Full_adder full_adder_3 (
    .Input_a(Input_a[2]), .Input_b(Input_b[2]), .Carry_in(full_adder_1_carry_out), .Sum(Sum[2]),
    .Carry_out(full_adder_3_carry_out));
  Full_adder full_adder_4 (
    .Input_a(Input_a[3]), .Input_b(Input_b[3]), .Carry_in(full_adder_3_carry_out), .Sum(Sum[3]),
    .Carry_out(Carry_out));
endmodule

module Full_adder (
  input  Input_a,
  input  Input_b,
  input  Carry_in,
  output Sum,
  output Carry_out
);

  wire half_adder_1_carry, half_adder_1_sum, half_adder_2_carry;

  Half_adder half_adder_1 (.Input_a(Input_a), .Input_b(Input_b), .Sum(half_adder_1_sum), .Carry(half_adder_1_carry));
  Half_adder half_adder_2 (.Input_a(half_adder_1_sum), .Input_b(Carry_in), .Sum(Sum), .Carry(half_adder_2_carry));
  or or_1 (Carry_out, half_adder_2_carry, half_adder_1_carry);
endmodule

module Half_adder (
  input  Input_a,
  input  Input_b,
  output Sum,
  output Carry
);

  xor xor_1 (Sum, Input_a, Input_b);
  and and_1 (Carry, Input_a, Input_b);
endmodule
