// Logisim project Program counter.circ as structural Verilog: 2 circuits, main circuit Program counter
module Program_counter (
  input  Load_data,
  input  Enable_count,
  input  Clear_count,
  input  Clock,
  input  [15:0] Data_input,
  output [15:0] Count_output
);

  wire n4_bit_counter_1_enable_carry, n4_bit_counter_2_enable_carry, n4_bit_counter_3_enable_carry;

  _4_Bit_counter u_4_bit_counter_1 (
    .Enable_count(Enable_count), .Count_output(Count_output[3:0]), .Load_data(Load_data),
    .Data_input(Data_input[3:0]), .Clock(Clock), .Clear_count(Clear_count),
    .Enable_carry(n4_bit_counter_1_enable_carry));
  _4_Bit_counter u_4_bit_counter_2 (
    .Enable_count(n4_bit_counter_1_enable_carry), .Count_output(Count_output[7:4]), .Load_data(Load_data),
    .Data_input(Data_input[7:4]), .Clock(Clock), .Clear_count(Clear_count),
    .Enable_carry(n4_bit_counter_2_enable_carry));
  _4_Bit_counter u_4_bit_counter_3 (
    .Enable_count(n4_bit_counter_2_enable_carry), .Count_output(Count_output[11:8]), .Load_data(Load_data),
    .Data_input(Data_input[11:8]), .Clock(Clock), .Clear_count(Clear_count),
    .Enable_carry(n4_bit_counter_3_enable_carry));
  _4_Bit_counter u_4_bit_counter_4 (
    .Enable_count(n4_bit_counter_3_enable_carry), .Count_output(Count_output[15:12]), .Load_data(Load_data),
    .Data_input(Data_input[15:12]), .Clock(Clock), .Clear_count(Clear_count));  // open: Enable_carry
endmodule

module _4_Bit_counter (
  input  Clock,
  input  Clear_count,
  input  Enable_count,
  input  Load_data,
  input  [3:0] Data_input,
  output [3:0] Count_output,
  output Enable_carry
);

  wire and_1_out, and_2_out, and_3_out, and_5_out, and_6_out, and_7_out, and_8_out;

  and and_1 (and_1_out, Count_output[1], and_2_out);
  T_Flip_Flop t_ff_1 (
    .clk(Clock), .T(Enable_count), .Q(Count_output[0]), .preset(and_5_out), .reset(Clear_count));  // open: Qn, en
  T_Flip_Flop t_ff_2 (
    .clk(Clock), .T(and_2_out), .Q(Count_output[1]), .preset(and_6_out), .reset(Clear_count));  // open: Qn, en
  and and_2 (and_2_out, Enable_count, Count_output[0]);
  T_Flip_Flop t_ff_3 (
    .clk(Clock), .T(and_1_out), .Q(Count_output[2]), .preset(and_7_out), .reset(Clear_count));  // open: Qn, en
  and and_3 (and_3_out, and_1_out, Count_output[2]);
  T_Flip_Flop t_ff_4 (
    .clk(Clock), .T(and_3_out), .Q(Count_output[3]), .preset(and_8_out), .reset(Clear_count));  // open: Qn, en
  and and_4 (Enable_carry, and_3_out, Count_output[3]);
  and and_5 (and_5_out, Load_data, Data_input[3]);
  and and_6 (and_6_out, Load_data, Data_input[2]);
  and and_7 (and_7_out, Load_data, Data_input[1]);
  and and_8 (and_8_out, Load_data, Data_input[0]);
endmodule
