// Logisim project Registers.circ as structural Verilog: 1 circuit, main circuit Register array
module Register_array (
);

  D_Flip_Flop d_ff_1 ();  // open: clk, D, Q, Qn, preset, en, reset
  D_Flip_Flop d_ff_2 ();  // open: clk, D, Q, Qn, preset, en, reset
  D_Flip_Flop d_ff_3 ();  // open: clk, D, Q, Qn, preset, en, reset
  D_Flip_Flop d_ff_4 ();  // open: clk, D, Q, Qn, preset, en, reset
  D_Flip_Flop d_ff_5 ();  // open: clk, D, Q, Qn, preset, en, reset
  D_Flip_Flop d_ff_6 ();  // open: clk, D, Q, Qn, preset, en, reset
  D_Flip_Flop d_ff_7 ();  // open: clk, D, Q, Qn, preset, en, reset
  D_Flip_Flop d_ff_8 ();  // open: clk, D, Q, Qn, preset, en, reset
  D_Flip_Flop d_ff_9 ();  // open: clk, D, Q, Qn, preset, en, reset
  D_Flip_Flop d_ff_10 ();  // open: clk, D, Q, Qn, preset, en, reset
  D_Flip_Flop d_ff_11 ();  // open: clk, D, Q, Qn, preset, en, reset
  D_Flip_Flop d_ff_12 ();  // open: clk, D, Q, Qn, preset, en, reset
  D_Flip_Flop d_ff_13 ();  // open: clk, D, Q, Qn, preset, en, reset
  D_Flip_Flop d_ff_14 ();  // open: clk, D, Q, Qn, preset, en, reset
  D_Flip_Flop d_ff_15 ();  // open: clk, D, Q, Qn, preset, en, reset
  D_Flip_Flop d_ff_16 ();  // open: clk, D, Q, Qn, preset, en, reset
endmodule
